// Logisim project IEClib_x32.circ as structural Verilog: 8 circuits, main circuit SUM
module SUM (
  input  in_1,
  input  [31:0] in_2,
  input  [31:0] in_3,
  output [31:0] out_4,
  output out_5
);

  Adder #(.width(32)) adder_1 (.a(in_2), .b(in_3), .out(out_4), .cin(in_1), .cout(out_5));
endmodule

module CMP (
  input  [31:0] in_1,
  input  [31:0] in_2,
  output out_3,
  output out_4,
  output out_5
);

  Comparator #(.width(32)) comparator_1 (.a(in_1), .b(in_2), .gt(out_3), .eq(out_4), .lt(out_5));
endmodule

module CT (
  input  in_1,
  input  in_2,
  input  [31:0] in_3,
  input  in_4,
  input  in_5,
  input  in_6,
  output [31:0] out_7,
  output out_8
);

  Counter #(.max('hffffffff), .width(32)) counter_1 (
    .load(in_2), .D(in_3), .count(in_4), .Q(out_7), .carry(out_8), .up(in_1), .clk(in_5), .clr(in_6));
endmodule

module BUFF (
  input  in_1,
  input  [31:0] in_2,
  output [31:0] out_3
);

  assign out_3 = in_1 ? in_2 : 32'bz;  // Controlled_Buffer controlled_buffer_1
endmodule

module RSH_REG (
  input  [31:0] in_1,
  input  in_2,
  input  in_3,
  input  in_4,
  input  in_5,
  input  in_6,
  output out_7,
  output [31:0] out_8
);

  Shift_Register #(.length(32)) shift_register_1 (
    .shift(in_3), .in(in_4), .clk(in_5), .out(out_7), .load(in_2), .clr(in_6), .d0(in_1[31]), .q0(out_8[31]),
    .d1(in_1[30]), .q1(out_8[30]), .d2(in_1[29]), .q2(out_8[29]), .d3(in_1[28]), .q3(out_8[28]),
    .d4(in_1[27]), .q4(out_8[27]), .d5(in_1[26]), .q5(out_8[26]), .d6(in_1[25]), .q6(out_8[25]),
    .d7(in_1[24]), .q7(out_8[24]), .d8(in_1[23]), .q8(out_8[23]), .d9(in_1[22]), .q9(out_8[22]),
    .d10(in_1[21]), .q10(out_8[21]), .d11(in_1[20]), .q11(out_8[20]), .d12(in_1[19]), .q12(out_8[19]),
    .d13(in_1[18]), .q13(out_8[18]), .d14(in_1[17]), .q14(out_8[17]), .d15(in_1[16]), .q15(out_8[16]),
    .d16(in_1[15]), .q16(out_8[15]), .d17(in_1[14]), .q17(out_8[14]), .d18(in_1[13]), .q18(out_8[13]),
    .d19(in_1[12]), .q19(out_8[12]), .d20(in_1[11]), .q20(out_8[11]), .d21(in_1[10]), .q21(out_8[10]),
    .d22(in_1[9]), .q22(out_8[9]), .d23(in_1[8]), .q23(out_8[8]), .d24(in_1[7]), .q24(out_8[7]),
    .d25(in_1[6]), .q25(out_8[6]), .d26(in_1[5]), .q26(out_8[5]), .d27(in_1[4]), .q27(out_8[4]),
    .d28(in_1[3]), .q28(out_8[3]), .d29(in_1[2]), .q29(out_8[2]), .d30(in_1[1]), .q30(out_8[1]), .d31(in_1[0]));  // open: q31

  assign out_8[0] = out_7;
endmodule

module LSH_REG (
  input  [31:0] in_1,
  input  in_2,
  input  in_3,
  input  in_4,
  input  in_5,
  input  in_6,
  output out_7,
  output [31:0] out_8
);

  Shift_Register #(.length(32)) shift_register_1 (
    .shift(in_3), .in(in_4), .clk(in_5), .out(out_7), .load(in_2), .clr(in_6), .d0(in_1[0]), .q0(out_8[0]),
    .d1(in_1[1]), .q1(out_8[1]), .d2(in_1[2]), .q2(out_8[2]), .d3(in_1[3]), .q3(out_8[3]), .d4(in_1[4]),
    .q4(out_8[4]), .d5(in_1[5]), .q5(out_8[5]), .d6(in_1[6]), .q6(out_8[6]), .d7(in_1[7]), .q7(out_8[7]),
    .d8(in_1[8]), .q8(out_8[8]), .d9(in_1[9]), .q9(out_8[9]), .d10(in_1[10]), .q10(out_8[10]),
    .d11(in_1[11]), .q11(out_8[11]), .d12(in_1[12]), .q12(out_8[12]), .d13(in_1[13]), .q13(out_8[13]),
    .d14(in_1[14]), .q14(out_8[14]), .d15(in_1[15]), .q15(out_8[15]), .d16(in_1[16]), .q16(out_8[16]),
    .d17(in_1[17]), .q17(out_8[17]), .d18(in_1[18]), .q18(out_8[18]), .d19(in_1[19]), .q19(out_8[19]),
    .d20(in_1[20]), .q20(out_8[20]), .d21(in_1[21]), .q21(out_8[21]), .d22(in_1[22]), .q22(out_8[22]),
    .d23(in_1[23]), .q23(out_8[23]), .d24(in_1[24]), .q24(out_8[24]), .d25(in_1[25]), .q25(out_8[25]),
    .d26(in_1[26]), .q26(out_8[26]), .d27(in_1[27]), .q27(out_8[27]), .d28(in_1[28]), .q28(out_8[28]),
    .d29(in_1[29]), .q29(out_8[29]), .d30(in_1[30]), .q30(out_8[30]), .d31(in_1[31]));  // open: q31

  assign out_8[31] = out_7;
endmodule

module USMAN (
  input  [31:0] in_1,
  input  in_2,
  input  in_3,
  input  in_4,
  output [31:0] out_5
);

  Register #(.width(32)) register_1 (.D(in_1), .en(in_2), .Q(out_5), .clk(in_3), .clr(in_4));
endmodule

module DTrigger (
  input  in_1,
  input  in_2,
  input  in_3,
  input  in_4,
  output out_5
);

  D_Flip_Flop d_ff_1 (.clk(in_1), .D(in_2), .Q(out_5), .preset(in_3), .reset(in_4));  // open: Qn
endmodule
